# Fritzing sketch arduino-scotch-mount-motor (saved by Fritzing 0.9.1b)
breadboards: 1

parts:
  Part1 = Arduino Uno (Rev3) - ICSP
  M1 = DC Motor
  IC1 = L293D [package=THT]
  S1 = Toggle Switch [package=THT]
  S2 = SWITCH-MOMENTARY-2 [package=tactile-switch-1101ne]

nets:
  N1: Part1.GND, IC1.0V, S2.1
  N2: Part1.5V, S1.L1
  N3: Part1.D9_PWM, IC1.In_2
  N4: Part1.D10_PWM/SS, IC1.In_1
  N5: Part1.D11_PWM/MOSI, IC1.Enable_1
  N6: Part1.D7, S2.2
  N7: M1.pin_1, IC1.Out_2_(_Controlled_by_Enable_1_)
  N8: M1.pin_2, IC1.Out_1_(_Controlled_by_Enable_1_)
  N9: IC1.+Vmotor, IC1.+V, S1.COM

// code stored in the sketch: arduino-scotch-mount-motor.ino
/*     -----------------------------------------------------------
 *     |  Arduino Scotch Mount Motor Drive                       |
 *     |  by: Kevin M. Kingsbury                                 |
 *     |  http://www.kevinkingsbury.com                          |
 *     -----------------------------------------------------------
 * 
 *  Instructable:
 * 
 */
//L293D motor driver chip. L293D IC
int enablePin = 11;  
int in1Pin = 10;
int in2Pin = 9;
int torque = 250; /* 0 to 255, for simple motors this is speed. 
For the motor I'm using this is more like a torque; low values stop, high stronger. */

//Reverse Direction Button: Tactile push switch
int switchPin = 7;

// Timing Delays to get the right rotation/min.
int onTime = 500;  //the number of milliseconds for the motor to turn on for
int offTime = 500; //the number of milliseconds for the motor to turn off for


void setup()
{
  pinMode(in1Pin, OUTPUT); 
  pinMode(in2Pin, OUTPUT);
  pinMode(enablePin, OUTPUT);
  pinMode(switchPin, INPUT_PULLUP);
}


void loop()                     // run over and over again
{
 motorOnAndOff();
}

void runMotor(int speed, boolean reverse)
{
  analogWrite(enablePin, speed);
  digitalWrite(in1Pin, ! reverse);
  digitalWrite(in2Pin, reverse);
}
void stopMotor()
{
  digitalWrite(in1Pin, 0);
  digitalWrite(in2Pin, 0);
}


void motorOnAndOff(){
  boolean reverse = digitalRead(switchPin);
  runMotor(torque, reverse);
  delay(onTime);                // waits for onTime milliseconds
  stopMotor();
  delay(offTime);               // waits for offTime milliseconds
}
